# Fritzing sketch Untitled Sketch (saved by Fritzing 0.9.3b)
breadboards: 1

parts:
  Часть1 = Arduino Uno (Rev3)
  R1 = Resistor [tolerance=±5% resistance=220 package=THT]
  R2 = Photocell (LDR) [package=THT]
  R3 = Trimmer Potentiometer [maximum_resistance=10kΩ package=THT]

nets:
  N1: Часть1.A0, R2.pin_1
  N2: Часть1.A1, R3.wiper
  N3: Часть1.5V, R3.leg1
  N4: Часть1.GND, R1.Pin_0, R3.leg2
  N5: R1.Pin_1, R2.pin_0
