# Fritzing sketch Untitled Sketch (saved by Fritzing 0.9.3b)
breadboards: 1

parts:
  Часть1 = Arduino Uno (Rev3)
  R1 = Resistor [tolerance=±5% resistance=220 package=THT]
  R2 = Resistor [tolerance=±5% resistance=220 package=THT]
  R3 = Resistor [tolerance=±5% resistance=220 package=THT]
  R4 = Resistor [tolerance=±5% resistance=220 package=THT]
  7_Segment1 = 7 Segment Display
  R5 = Resistor [tolerance=±5% resistance=220 package=THT]
  R6 = Resistor [tolerance=±5% resistance=220 package=THT]
  R7 = Resistor [tolerance=±5% resistance=220 package=THT]  # not connected

nets:
  N1: Часть1.D8, R1.Pin_0
  N2: Часть1.D2, R5.Pin_0
  N3: Часть1.D3_PWM, R6.Pin_1
  N4: Часть1.D5_PWM, R4.Pin_1
  N5: Часть1.D6_PWM, R3.Pin_1
  N6: Часть1.D7, R2.Pin_0
  N7: R1.Pin_1, 7_Segment1.Segment_G, 7_Segment1.Segment_F
  N8: R4.Pin_0, 7_Segment1.Segment_B, 7_Segment1.Segment_A
  N9: 7_Segment1.Segment_D, R5.Pin_1
  N10: 7_Segment1.Segment_DP, R6.Pin_0
