# Fritzing sketch Untitled Sketch 2 (saved by Fritzing 0.9.3b)
breadboards: 1

parts:
  Часть1 = Arduino Uno (Rev3)
  D1 = LED_BARGRAPH_10 [package=led_bargaph_10]
  R1 = Resistor [tolerance=±5% resistance=220 package=THT]
  R2 = Resistor [tolerance=±5% resistance=220 package=THT]
  R3 = Resistor [tolerance=±5% resistance=220 package=THT]
  R4 = Resistor [tolerance=±5% resistance=220 package=THT]
  R5 = Resistor [tolerance=±5% resistance=220 package=THT]
  R6 = Resistor [tolerance=±5% resistance=220 package=THT]
  R7 = Resistor [tolerance=±5% resistance=220 package=THT]
  R8 = Resistor [tolerance=±5% resistance=220 package=THT]
  R9 = Resistor [tolerance=±5% resistance=220 package=THT]

nets:
  N1: Часть1.D8, D1.D_C
  N2: Часть1.D9_PWM, D1.C_C
  N3: Часть1.D10_PWM/SS, D1.B_C
  N4: Часть1.D11_PWM/MOSI, D1.A_C
  N5: Часть1.D2, D1.J_C
  N6: Часть1.D3_PWM, D1.I_C
  N7: Часть1.D4, D1.H_C
  N8: Часть1.D5_PWM, D1.G_C
  N9: Часть1.D6_PWM, D1.F_C
  N10: Часть1.D7, D1.E_C
  N11: Часть1.GND, R1.Pin_0, R2.Pin_0, R3.Pin_0, R4.Pin_0, R5.Pin_0, R6.Pin_0, R7.Pin_0, R8.Pin_0, R9.Pin_0
  N12: D1.A_A, R1.Pin_1
  N13: D1.B_A, R2.Pin_1
  N14: D1.C_A, R3.Pin_1
  N15: D1.E_A, R4.Pin_1
  N16: D1.F_A, R5.Pin_1
  N17: D1.G_A, R6.Pin_1
  N18: D1.H_A, R7.Pin_1
  N19: D1.I_A, R8.Pin_1
  N20: D1.J_A, R9.Pin_1
