# Fritzing sketch Untitled Sketch (saved by Fritzing 0.9.3b)
breadboards: 1

parts:
  Часть1 = Arduino Uno (Rev3)
  LED1 = LED - 5mm [color="Red (633nm)" package="5 mm [THT]"]
  R1 = Resistor [tolerance=±5% resistance=220 package=THT]
  R2 = Trimmer Potentiometer [maximum_resistance=10kΩ package=THT]

nets:
  N1: Часть1.A0, R2.wiper
  N2: Часть1.D9_PWM, R1.Pin_0
  N3: Часть1.5V, R2.leg1
  N4: Часть1.GND, LED1.anode, R2.leg2
  N5: LED1.cathode, R1.Pin_1
