# Fritzing sketch Untitled Sketch.fzz usb-rgb (saved by Fritzing 0.9.3b)
breadboards: 1

parts:
  Часть1 = Arduino Uno (Rev3)
  R1 = Resistor [tolerance=±5% resistance=220 package=THT]
  R2 = Resistor [tolerance=±5% resistance=220 package=THT]
  R3 = Resistor [tolerance=±5% resistance=220 package=THT]
  LED1 = RGB LED (com. cathode, rgb) [package="5 mm [THT]"]

nets:
  N1: Часть1.D9_PWM, R1.Pin_0
  N2: Часть1.D10_PWM/SS, R2.Pin_1
  N3: Часть1.D11_PWM/MOSI, R3.Pin_1
  N4: Часть1.VIN, LED1.green_anode
  N5: R1.Pin_1, LED1.blue_anode
  N6: R2.Pin_0, LED1.common_cathode
  N7: R3.Pin_0, LED1.red_anode
