# Fritzing sketch Untitled Sketch 2 (saved by Fritzing 0.9.3b)
circuit board: 9.04025cm x 6.20232cm
breadboards: 1

parts:
  Часть1 = Arduino Uno (Rev3)
  R1 = Resistor [tolerance=±5% resistance=220 package=THT]
  R2 = Resistor [tolerance=±5% resistance=220 package=THT]
  R3 = Resistor [tolerance=±0.05% resistance=220 package=THT]
  LED2 = LED - 5mm [color="Red (633nm)" package="5 mm [THT]"]
  LED1 = smd LED [color="Red (633nm)" package="0603 [SMD]"]
  LED1_2 = smd LED [color="Red (633nm)" package="0805 [SMD]"]
  LED1_3 = smd LED [color="Red (633nm)" package="0603 [SMD]"]
  LED3 = LED - 5mm [color="Red (633nm)" package="5 mm [THT]"]

nets:
  N1: Часть1.D10_PWM/SS, R3.Pin_1
  N2: Часть1.D11_PWM/MOSI, R2.Pin_1
  N3: Часть1.D12/MISO, R1.Pin_1
  N4: Часть1.GND, LED2.cathode, LED1.cathode, LED1_2.cathode, LED1_3.cathode, LED3.cathode
  N5: R1.Pin_0, LED1.anode, LED1_2.anode, LED1_3.anode
  N6: R2.Pin_0, LED2.anode
  N7: R3.Pin_0, LED3.anode
